# Fritzing sketch arduino (saved by Fritzing 0.9.2b)
breadboards: 1

parts:
  Componente1 = Arduino Uno (Rev3)
  T1 = LM35 Temperature Sensor [package="TO92 [THT]"]
  R1 = Photocell (LDR) [package=THT]
  R3 = Resistor [tolerance=±5% resistance=10k package=THT]
  R4 = Resistor [tolerance=±5% resistance=10k package=THT]

nets:
  N1: Componente1.A0, T1.Vout
  N2: Componente1.A1, R1.pin_1, R3.Pin_0
  N3: Componente1.GND, T1.+Vs, R3.Pin_1
  N4: Componente1.5V, R1.pin_0, R4.Pin_1
  N5: T1.GND, R4.Pin_0
